# Fritzing sketch receiver (saved by Fritzing 0.9.3b)

parts:
  Part1 = Adafruit Motor/Stepper/Servo Shield [part_number="Adafruit #1438"]
  S7 = Toggle Switch spst [package=THT]
  M2 = DC Motor
  M3 = DC Motor
  M5 = DC Motor
  M6 = DC Motor
  Part2 = NRF24L01+ Breakout Board

nets:
  N1: Part1.M2A, M6.pin_1
  N2: Part1.M2B, M6.pin_2
  N3: Part1.M1B, M3.pin_1
  N4: Part1.M1A, M3.pin_2
  N5: Part1.M3A, M2.pin_2
  N6: Part1.M3B, M2.pin_1
  N7: Part1.M4B, M5.pin_2
  N8: Part1.M4A, M5.pin_1
  GND: Part1.GND, Part2.GND
  N9: Part1.VMOTOR, S7.COM
  +3V3: Part1.+3V3, Part2.VCC
  N10: Part1.D8, Part2.CE
  N11: Part1.D9, Part2.CS
  N12: Part1.D11, Part2.MOSI
  N13: Part1.D12, Part2.MISO
  N14: Part1.D13, Part2.SCK

notes:
  Battery 12Volts

custom parts:
  Adafruit Motor/Stepper/Servo Shield: The original Adafruit Motorshield kit is one of our most beloved kits, which is why we decided to make something even better. We have upgraded the shield kit to make the bestest, easiest way to drive DC and Stepper motors. This shield will make quick work of your next robotics project! We kept the ability to drive up to 4 DC motors or 2 stepper motors, but added many improvements: Instead of a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
  Toggle Switch spst: Toggle Switch single pole single throw
